# Fritzing sketch pump-relay (saved by Fritzing 0.9.3b)
breadboards: 1

parts:
  Onderdeel1 = Adafruit HUZZAH32 ESP32 Feather [part_number="Adafruit #3405"]
  Onderdeel2 = Adafruit Latching Mini Relay FeatherWing [part_number="Adafruit #2923"]
  J1 = Power Jack [package=power_jack_smd]
  M1 = DC Motor

nets:
  GND: Onderdeel1.GND, Onderdeel2.GND
  3.3V: Onderdeel1.3.3V, Onderdeel2.3.3V
  N1: Onderdeel1.IO12_A11, Onderdeel2.C, Onderdeel2.SET
  N2: Onderdeel1.IO27_A10, Onderdeel2.E, Onderdeel2.UNSET
  N3: Onderdeel2.NO, M1.pin_1
  N4: Onderdeel2.COM, J1.PWR
  N5: J1.GND, M1.pin_2

notes:
  On my Feather Huzzah, the actual pins to call from code are: 12 --> set, 13 --> unset

custom parts:
  Adafruit Latching Mini Relay FeatherWing: A Feather board without ambition is a Feather board without FeatherWings! This is the Latching Mini Relay FeatherWing. It gives you power to control, and control over power. Put simply, you can now turn on and off lamps, fans, solenoids, and other small appliances that run on up to 250VAC or DC power using any Feather board. The are two 'flavors' of these FeatherWings, this is the Latching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
